# Fritzing sketch MPL115A1_raspi (saved by Fritzing 0.9.4)
breadboards: 1

parts:
  Raspberry_Pi_1 = Raspberry Pi 3 [part_number=RPI-3-V1.2]
  U2 = _h3_MPL115A1 (SPI) and MPL115A2 (I2C) Miniature Digital Barometer__h3_ [package=lga8]
  C1 = Capacitor [package=cap-pth-small-kit]

nets:
  N1: Raspberry_Pi_1.GPIO22, U2.VDD, U2.SHDN
  N2: Raspberry_Pi_1.3V3, U2.SDA_DIN
  N3: Raspberry_Pi_1.GPIO10, U2.NC_DOUT
  N4: Raspberry_Pi_1.GPIO9, U2.SCLK
  N5: Raspberry_Pi_1.GPIO11, U2.GND, C1.2
  N6: Raspberry_Pi_1.GPIO25, U2.RST_CS
  N7: U2.CAP, C1.1
